# Fritzing sketch droid_accessory_base (saved by Fritzing 0.8.5b)

parts:
  Part1 = Arduino USB Host Shield
  U1 = atmega328 [package=dip]
  R1 = Resistor [tolerance=±5% resistance=1k package=THT]
  C1 = Ceramic Capacitor [capacitance=22pF package="100 mil [THT, multilayer]"]
  C2 = Ceramic Capacitor [capacitance=22pF package="100 mil [THT, multilayer]"]
  Y1 = CRYSTAL [package=crystal-smd-5x3]
  J1 = female pin header, 6 pins [form="♀ (female)"]

nets:
  N1: Part1.RESET, Part1.N$133, U1.D7
  N2: Part1.GPX, Part1.N$118, U1.D8
  N3: Part1.INT, Part1.N$103, U1.D9_(PWM)
  N4: Part1.SS, Part1.N$104, U1.D10_(PWM)
  N5: Part1.MOSI, Part1.N$105, U1.D11_(PWM)
  N6: Part1.MISO, Part1.N$106, U1.D12
  N7: Part1.SCK, Part1.N$107, U1.D13
  GND: Part1.GND, Part1.N$54, Part1.N$55, Part1.N$78, Part1.N$84, Part1.N$125, Part1.N$126, U1.GND, C1.1, C2.0, J1.pin1, J1.pin2
  N8: Part1.N$26, U1.A5
  N9: Part1.N$29, Part1.N$37, U1.RESET, R1.Pin_0
  N10: Part1.N$33, U1.A4
  N11: Part1.N$36, U1.D0_(RX)
  N12: Part1.N$43, Part1.N$45, Part1.N$137, U1.XLAT1, C1.0, Y1.2
  N13: Part1.N$47, Part1.N$124, Part1.N$136, U1.XLAT2, C2.1, Y1.1
  N14: Part1.N$56, Part1.N$68, U1.D2, J1.pin3
  N15: Part1.N$57, Part1.N$75, U1.D3_(PWM), J1.pin4
  N16: Part1.N$58, Part1.N$134, U1.D6_(PWM), J1.pin5
  N17: Part1.N$59, Part1.N$135, U1.D5_(PWM), J1.pin6
  N18: Part1.N$60, U1.A3
  N19: Part1.N$63, U1.D1_(TX)
  N20: Part1.N$71, U1.A2
  N21: Part1.N$72, U1.A1
  N22: Part1.N$79, Part1.N$87, U1.VCC, R1.Pin_1
  N23: Part1.N$80, U1.D4
  N24: Part1.N$83, U1.A0
  N25: Part1.N$108, U1.AVCC
  N26: Part1.N$109, U1.AREF
