# Fritzing sketch home_automation_controller (saved by Fritzing 0.8.5b)
circuit board: 3.81451cm x 3.30858cm
breadboards: 1

parts:
  R1 = Resistor [tolerance=±5% resistance=1k package=THT]
  R2 = Resistor [tolerance=±5% resistance=1M package=THT]
  R3 = Resistor [tolerance=±5% resistance=1k package=THT]
  R4 = Resistor [tolerance=±5% resistance=100k package=THT]
  R5 = Resistor [tolerance=±5% resistance=33k package=THT]
  C1 = Electrolytic Capacitor [capacitance=1µF voltage=16V package="100 mil [THT, electrolytic]"]
  D1 = Rectifier Diode [part_number=1N4001 package="300 mil [THT]"]
  5V(+) = female pin header, 1 pin [form="♀ (female)"]
  5V(-) = female pin header, 1 pin [form="♀ (female)"]
  Audio_In = female pin header, 2 pins [form="♀ (female)"]
  A4 = male pin header, 1 pin [form="♂ (male)"]
  Gnd = male pin header, 1 pin [form="♂ (male)"]
  5Vout = male pin header, 1 pin [form="♂ (male)"]
  IC3 = IC, DIP package, 8 pins [chip_label=IC part_number=LM833N]
  C2 = Ceramic Capacitor [capacitance=220nF package="200 mil [THT, multilayer]"]

nets:
  N1: R1.Pin_0, Audio_In.pin2
  N2: R1.Pin_1, C1.+
  N3: R2.Pin_0, D1.anode, IC3.pin7
  N4: R2.Pin_1, R3.Pin_0, IC3.pin5
  GND: R3.Pin_1, R4.Pin_1, R5.Pin_1, 5V(+).pin1, Audio_In.pin1, Gnd.pin1, C2.1
  N5: R4.Pin_0, D1.cathode, A4.pin1, C2.0
  N6: R5.Pin_0, C1.-, IC3.pin6
  N7: 5V(-).pin1, IC3.pin4
  N8: 5Vout.pin1, IC3.pin8
