# Fritzing sketch smart_thermostat (saved by Fritzing 0.8.5b)
circuit board: 6.48181cm x 7.7696cm
breadboards: 2

parts:
  R2 = Resistor [tolerance=±5% resistance=470 package=THT]
  R3 = Resistor [tolerance=±5% resistance=270 package=THT]
  R4 = Resistor [tolerance=±5% resistance=1k package=THT]
  R5 = Resistor [tolerance=±5% resistance=4.7k package=THT]
  C2 = Ceramic Capacitor [capacitance=22pF package="100 mil [THT, multilayer]"]
  D1 = Rectifier Diode [part_number=1N4001 package="300 mil [THT]"]
  X1 = Crystal [frequency="16 Mhz" package=THT]
  U1 = atmega328 [package=dip]
  T1 = NPN-Transistor [part_number=BC548 package="TO92 [THT]"]
  Red_LED = LED - 5mm [color="Red (633nm)" package="5 mm [THT]"]
  IC1 = DS18B20 [part_number=DS18B20 chip_label=IC package="SIP (Single Inline) [THT]"]
  R1_Set_Temp = Rotary Potentiometer (Small) [maximum_resistance=100kΩ package=THT]
  Furnace = female pin header, 2 pins [form="♀ (female)"]
  5Vin = female pin header, 2 pins [form="♀ (female)"]
  5V_Relay = RELAY [package=relay-g5q]
  RF_Receiver = RF-LINK_RX [package=rf-link_rx]
  S1_Override = Toggle Switch [package=THT]
  C1 = Ceramic Capacitor [capacitance=100nF package="200 mil [THT, multilayer]"]
  C3 = Ceramic Capacitor [capacitance=22pF package="200 mil [THT, multilayer]"]

nets:
  N1: R2.Pin_0, T1.B
  N2: R2.Pin_1, U1.D7
  N3: R3.Pin_0, U1.D8
  N4: R3.Pin_1, Red_LED.anode
  5V: R4.Pin_0, R5.Pin_0, D1.cathode, IC1.VCC, R1_Set_Temp.leg2, 5Vin.pin2, 5V_Relay.COIL1, RF_Receiver.+5V, C1.0
  N5: R4.Pin_1, U1.RESET
  N6: R5.Pin_1, U1.D10_(PWM), IC1.Data
  GND: C2.0, U1.GND, T1.E, Red_LED.cathode, IC1.Gnd, R1_Set_Temp.leg1, 5Vin.pin1, RF_Receiver.GND, S1_Override.COM, C1.1, C3.1
  N7: C2.1, X1.pin_0, U1.XLAT1
  N8: D1.anode, T1.C, 5V_Relay.COIL2
  N9: X1.pin_1, U1.XLAT2, C3.0
  N10: U1.D9_(PWM), S1_Override.L2
  N11: U1.D11_(PWM), RF_Receiver.DATA
  N12: U1.A0, R1_Set_Temp.wiper
  N13: Furnace.pin1, 5V_Relay.MAIN
  N14: Furnace.pin2, 5V_Relay.NO

custom parts:
  DS18B20: Dallas 1-wire digital temperature sensor
